# Fritzing sketch 02-smoothing (saved by Fritzing 0.9.3b)
breadboards: 1

parts:
  Part1 = Arduino Uno (Rev3)
  J1 = Basic Servo
  Q1 = LTR-301 [package=ltr-301]
  R2 = Resistor [tolerance=±5% resistance=10k package=THT]

nets:
  N1: Part1.A0, Q1.C, R2.Pin_0
  N2: Part1.D3_PWM, J1.pulse
  5V: Part1.5V, J1.vcc, Q1.E
  N3: Part1.GND, R2.Pin_1
