# Fritzing sketch 01-arm-position (saved by Fritzing 0.9.3b)
breadboards: 1

parts:
  Part1 = Arduino Uno (Rev3)
  J1 = Basic Servo
  J2 = Basic Servo
  R1 = Rotary Potentiometer (Small) [maximum_resistance=100kΩ package=THT]
  R2 = Rotary Potentiometer (Small) [maximum_resistance=100kΩ package=THT]

nets:
  N1: Part1.A0, R1.wiper
  N2: Part1.A1, R2.wiper
  N3: Part1.D3_PWM, J1.pulse
  N4: Part1.D5_PWM, J2.pulse
  VCC: Part1.5V, J1.vcc, J2.vcc, R1.leg1, R2.leg1
  GND: Part1.GND, J2.gnd, R1.leg2, R2.leg2
