# Fritzing sketch 02-send-pot-button (saved by Fritzing 0.9.3b)
breadboards: 1

parts:
  Part1 = Arduino Uno (Rev3)
  R2 = Rotary Potentiometer (Small) [maximum_resistance=100kΩ package=THT]
  S1 = Pushbutton [package="[THT]"]
  R3 = Resistor [tolerance=±5% resistance=10k package=THT]

nets:
  N1: Part1.A0, R2.wiper
  N2: Part1.5V, R2.leg1, S1.Pin_3, S1.Pin_4
  N3: Part1.GND, R2.leg2, R3.Pin_1
  N4: S1.Pin_1, S1.Pin_2, R3.Pin_0
